# Fritzing sketch Obstacle Fritzing (saved by Fritzing 0.9.3b)

parts:
  S1 = H-Bridge with L298N
  M1 = DC Motor
  M2 = DC Motor
  M3 = DC Motor
  J1 = Basic Servo
  hc-sr1 = hc-sr04
  M4 = DC Motor
  Parça1 = Arduino Uno (Rev3)
  VCC1 = 4 x AAA Battery Mount
  VCC2 = Battery block 9V  # not connected

nets:
  N1: S1.12V, VCC1.+
  GND: S1.GND, J1.gnd, hc-sr1.GND, Parça1.GND, VCC1.-
  N2: S1.IN1, Parça1.D10_PWM/SS
  N3: S1.IN2, Parça1.D11_PWM/MOSI
  N4: S1.IN3, Parça1.D9_PWM
  N5: S1.IN4, Parça1.D8
  N6: S1.M1-01, M3.pin_1
  N7: S1.M1-02, M1.pin_1, M3.pin_2
  N8: S1.M2-01, M2.pin_2, M4.pin_1
  N9: S1.M2-02, M2.pin_1, M4.pin_2
  N10: J1.pulse, Parça1.D7
  VCC: hc-sr1.VCC, Parça1.5V
  N11: hc-sr1.Trig, Parça1.D5_PWM
  N12: hc-sr1.Echo, Parça1.D6_PWM

notes:
  9 V batarya Arduinoyu beslemek için
  Sağ Motorlar
  Sol Motorlar
  4 adet Kalem Pil Motor Sürücüyü beslemek için Sırasıyla Bağlantılar:
  Kırmızı:L298N +12V
  Siyah:L298N Gnd
  Hc-SR04 Ultrasonik Sensör Sırasıyla Bağlantılar:
  VCC=5V
  Trig=Pin 5
  Echo=Pin 6
  Gnd=Arduino Gnd
  SG90 Servo Motor Sırasıyla Bağlantılar:
  Siyah: Arduino Gnd
  Kırmızı:5V
  Sarı:Pin 7
  L298N H-Bridge Motor Sürücüsü Sırasıyla Bağlantılar:
  EnA=Bağlantı Yok
  ln1=Pin 10
  ln2=Pin 11
  ln3=Pin 9
  ln4=Pin 8
  EnB=Bağlantı Yok
  +5V=Servo 5V
  Gnd=Arduino Gnd

custom parts:
  H-Bridge with L298N: h-bridge
